// Logisim project ULA.circ as structural Verilog: 5 circuits, main circuit main
module main (
  input  [31:0] Entrada_A,
  input  [31:0] Entrada_B,
  input  [4:0] Seletor,
  output out_4,
  output [31:0] \Saída_S 
);

  wire overflowcontroler_1_overflow, undriven, undriven_2, undriven_3, undriven_4, undriven_5, undriven_6,
       undriven_7, undriven_8, undriven_9, undriven_10, undriven_11, undriven_12, undriven_13, undriven_14,
       undriven_15, undriven_16, undriven_17, undriven_18, undriven_19, undriven_20, undriven_21,
       undriven_22, undriven_23, undriven_24, undriven_25, undriven_26, undriven_27, undriven_28,
       undriven_29, undriven_30, undriven_31;

  Celula celula_1 (
    .Cin(undriven), .SLL(Entrada_A[29]), .b(Entrada_B[30]), .a(Entrada_A[30]), .Seletor(Seletor),
    .S(\Saída_S [30]), .SRL(Entrada_A[31]), .Cout(Entrada_A[31]));
  Celula celula_2 (
    .Cin(undriven_3), .SLL(Entrada_A[30]), .b(Entrada_B[31]), .a(Entrada_A[31]), .Seletor(Seletor),
    .S(\Saída_S [31]), .SRL(1'b0), .Cout(undriven));
  Celula celula_3 (
    .Cin(Entrada_A[31]), .SLL(Entrada_A[27]), .b(Entrada_B[28]), .a(Entrada_A[28]), .Seletor(Seletor),
    .S(\Saída_S [28]), .SRL(Entrada_A[29]), .Cout(undriven_4));
  Celula celula_4 (
    .Cin(undriven_2), .SLL(Entrada_A[28]), .b(Entrada_B[29]), .a(Entrada_A[29]), .Seletor(Seletor),
    .S(\Saída_S [29]), .SRL(Entrada_A[30]), .Cout(undriven_3));
  Celula celula_5 (
    .Cin(undriven_4), .SLL(Entrada_A[25]), .b(Entrada_B[26]), .a(Entrada_A[26]), .Seletor(Seletor),
    .S(\Saída_S [26]), .SRL(Entrada_A[27]), .Cout(undriven_5));
  Celula celula_6 (
    .Cin(undriven_6), .SLL(Entrada_A[26]), .b(Entrada_B[27]), .a(Entrada_A[27]), .Seletor(Seletor),
    .S(\Saída_S [27]), .SRL(Entrada_A[28]), .Cout(undriven_2));
  Celula celula_7 (
    .Cin(undriven_5), .SLL(Entrada_A[23]), .b(Entrada_B[24]), .a(Entrada_A[24]), .Seletor(Seletor),
    .S(\Saída_S [24]), .SRL(Entrada_A[25]), .Cout(undriven_7));
  Celula celula_8 (
    .Cin(undriven_9), .SLL(Entrada_A[24]), .b(Entrada_B[25]), .a(Entrada_A[25]), .Seletor(Seletor),
    .S(\Saída_S [25]), .SRL(Entrada_A[26]), .Cout(undriven_6));
  Celula celula_9 (
    .Cin(undriven_7), .SLL(Entrada_A[21]), .b(Entrada_B[23]), .a(Entrada_A[22]), .Seletor(Seletor),
    .S(\Saída_S [22]), .SRL(Entrada_A[23]), .Cout(undriven_8));
  Celula celula_10 (
    .Cin(undriven_10), .SLL(Entrada_A[22]), .b(Entrada_B[22]), .a(Entrada_A[23]), .Seletor(Seletor),
    .S(\Saída_S [23]), .SRL(Entrada_A[24]), .Cout(undriven_9));
  Celula celula_11 (
    .Cin(undriven_8), .SLL(Entrada_A[19]), .b(Entrada_B[21]), .a(Entrada_A[20]), .Seletor(Seletor),
    .S(\Saída_S [20]), .SRL(Entrada_A[21]), .Cout(undriven_11));
  Celula celula_12 (
    .Cin(undriven_14), .SLL(Entrada_A[20]), .b(Entrada_B[20]), .a(Entrada_A[21]), .Seletor(Seletor),
    .S(\Saída_S [21]), .SRL(Entrada_A[22]), .Cout(undriven_10));
  Celula celula_13 (
    .Cin(undriven_11), .SLL(Entrada_A[17]), .b(Entrada_B[19]), .a(Entrada_A[18]), .Seletor(Seletor),
    .S(\Saída_S [18]), .SRL(Entrada_A[19]), .Cout(undriven_13));
  Celula celula_14 (
    .Cin(undriven_12), .SLL(Entrada_A[18]), .b(Entrada_B[18]), .a(Entrada_A[19]), .Seletor(Seletor),
    .S(\Saída_S [19]), .SRL(Entrada_A[20]), .Cout(undriven_14));
  Celula celula_15 (
    .Cin(undriven_13), .SLL(Entrada_A[15]), .b(Entrada_B[17]), .a(Entrada_A[16]), .Seletor(Seletor),
    .S(\Saída_S [16]), .SRL(Entrada_A[17]), .Cout(undriven_16));
  Celula celula_16 (
    .Cin(undriven_15), .SLL(Entrada_A[16]), .b(Entrada_B[16]), .a(Entrada_A[17]), .Seletor(Seletor),
    .S(\Saída_S [17]), .SRL(Entrada_A[18]), .Cout(undriven_12));
  Celula celula_17 (
    .Cin(undriven_16), .SLL(Entrada_A[13]), .b(Entrada_B[15]), .a(Entrada_A[14]), .Seletor(Seletor),
    .S(\Saída_S [14]), .SRL(Entrada_A[15]), .Cout(undriven_17));
  Celula celula_18 (
    .Cin(undriven_20), .SLL(Entrada_A[14]), .b(Entrada_B[14]), .a(Entrada_A[15]), .Seletor(Seletor),
    .S(\Saída_S [15]), .SRL(Entrada_A[16]), .Cout(undriven_15));
  Celula celula_19 (
    .Cin(undriven_17), .SLL(Entrada_A[11]), .b(Entrada_B[13]), .a(Entrada_A[12]), .Seletor(Seletor),
    .S(\Saída_S [12]), .SRL(Entrada_A[13]), .Cout(undriven_19));
  Celula celula_20 (
    .Cin(undriven_18), .SLL(Entrada_A[12]), .b(Entrada_B[12]), .a(Entrada_A[13]), .Seletor(Seletor),
    .S(\Saída_S [13]), .SRL(Entrada_A[14]), .Cout(undriven_20));
  Celula celula_21 (
    .Cin(undriven_19), .SLL(Entrada_A[9]), .b(Entrada_B[11]), .a(Entrada_A[10]), .Seletor(Seletor),
    .S(\Saída_S [10]), .SRL(Entrada_A[11]), .Cout(undriven_22));
  Celula celula_22 (
    .Cin(undriven_21), .SLL(Entrada_A[10]), .b(Entrada_B[10]), .a(Entrada_A[11]), .Seletor(Seletor),
    .S(\Saída_S [11]), .SRL(Entrada_A[12]), .Cout(undriven_18));
  Celula celula_23 (
    .Cin(undriven_22), .SLL(Entrada_A[7]), .b(Entrada_B[9]), .a(Entrada_A[8]), .Seletor(Seletor),
    .S(\Saída_S [8]), .SRL(Entrada_A[9]), .Cout(undriven_24));
  Celula celula_24 (
    .Cin(undriven_23), .SLL(Entrada_A[8]), .b(Entrada_B[8]), .a(Entrada_A[9]), .Seletor(Seletor),
    .S(\Saída_S [9]), .SRL(Entrada_A[10]), .Cout(undriven_21));
  Celula celula_25 (
    .Cin(undriven_24), .SLL(Entrada_A[5]), .b(Entrada_B[7]), .a(Entrada_A[6]), .Seletor(Seletor),
    .S(\Saída_S [6]), .SRL(Entrada_A[7]), .Cout(undriven_25));
  Celula celula_26 (
    .Cin(undriven_27), .SLL(Entrada_A[6]), .b(Entrada_B[6]), .a(Entrada_A[7]), .Seletor(Seletor),
    .S(\Saída_S [7]), .SRL(Entrada_A[8]), .Cout(undriven_23));
  Celula celula_27 (
    .Cin(undriven_25), .SLL(Entrada_A[3]), .b(Entrada_B[5]), .a(Entrada_A[4]), .Seletor(Seletor),
    .S(\Saída_S [4]), .SRL(Entrada_A[5]), .Cout(undriven_26));
  Celula celula_28 (
    .Cin(undriven_30), .SLL(Entrada_A[4]), .b(Entrada_B[4]), .a(Entrada_A[5]), .Seletor(Seletor),
    .S(\Saída_S [5]), .SRL(Entrada_A[6]), .Cout(undriven_27));
  Celula celula_29 (
    .Cin(undriven_26), .SLL(Entrada_A[1]), .b(Entrada_B[3]), .a(Entrada_A[2]), .Seletor(Seletor),
    .S(\Saída_S [2]), .SRL(Entrada_A[3]), .Cout(undriven_29));
  Celula celula_30 (
    .Cin(undriven_28), .SLL(Entrada_A[2]), .b(Entrada_B[2]), .a(Entrada_A[3]), .Seletor(Seletor),
    .S(\Saída_S [3]), .SRL(Entrada_A[4]), .Cout(undriven_30));
  Celula celula_31 (
    .Cin(undriven_29), .SLL(1'b0), .b(Entrada_B[1]), .a(Entrada_A[0]), .Seletor(Seletor), .S(\Saída_S [0]),
    .SRL(Entrada_A[1]), .Cout(undriven_31));
  Celula celula_32 (
    .Cin(1'b0), .SLL(Entrada_A[0]), .b(Entrada_B[0]), .a(Entrada_A[1]), .Seletor(Seletor), .S(\Saída_S [1]),
    .SRL(Entrada_A[2]), .Cout(undriven_28));
  OverFlowControler overflowcontroler_1 (
    .Overflow(overflowcontroler_1_overflow), .Cin(undriven_31), .Seletor(Seletor), .a(Entrada_A[0]),
    .b(Entrada_B[1]), .s(\Saída_S [0]));

  // Notes on the sheet:
  //   00000=AND
  //   00001=OR
  //   00010=XOR
  //   00011=NAND
  //   00100=SOMA INT
  //   00101=SOMA NAT
  //   00110=SUBTRAIR
  //   00111=DESLOCAMENTO ESQUERDA
  //   01000=DESLOCAMENTO DIREITA
  //   1
  //   Overflow
endmodule

module Celula (
  input  Cin,
  input  SLL,
  input  SRL,
  input  b,
  input  a,
  input  Cout,
  input  [4:0] Seletor,
  output S
);

  wire and_1_out, and_2_out, nand_1_out, or_1_out, Somador_s, Somador_vai1, Subtrator_s, Subtrator_vai1,
       xor_1_out;

  and and_1 (and_1_out, a, b);
  or or_1 (or_1_out, a, b);
  xor xor_1 (xor_1_out, a, b);
  nand nand_1 (nand_1_out, a, b);
  Somador Somador (.a(a), .b(b), .Vem1(Cin), .Vai1(Somador_vai1), .S(Somador_s));
  Subtrator Subtrator (.a(a), .b(b), .Vem1(Cin), .Vai1(Subtrator_vai1), .S(Subtrator_s));
  Multiplexer #(.enable("false")) multiplexer_1 (.in0(Somador_vai1), .in1(Subtrator_vai1), .out(Cout), .sel(and_2_out));
  and and_2 (and_2_out, ~Seletor[0], Seletor[1], Seletor[2], ~Seletor[3], ~Seletor[4]);  // AND_Gate
  Multiplexer #(.select(5), .enable("false")) multiplexer_2 (
    .in0(and_1_out), .in1(or_1_out), .in2(xor_1_out), .in3(nand_1_out), .in4(Somador_s), .in5(Somador_s),
    .in6(Subtrator_s), .in7(SLL), .in8(SRL), .out(S), .sel(Seletor));  // open: in9, in10, in11, in12, in13, in14, in15, in16, in17, in18, in19, in20, in21, in22, in23, in24, in25, in26, in27, in28, in29, in30, in31

  // Notes on the sheet:
  //   00000=AND
  //   00001=OR
  //   00010=XOR
  //   00011=NAND
  //   00100=SOMA INT
  //   00101=SOMA NAT
  //   00110=SUBTRATOR
  //   00111=DESLOCAMENTO ESQUERDA
  //   01000=DESLOCAMENTO DIREITA
endmodule

module OverFlowControler (
  input  Cin,
  input  a,
  input  b,
  input  s,
  input  [4:0] Seletor,
  output Overflow
);

  wire and_1_out, and_2_out, and_3_out, or_1_out;

  Multiplexer #(.enable("false")) multiplexer_1 (.in0(Cin), .in1(or_1_out), .out(Overflow), .sel(and_1_out));
  and and_1 (and_1_out, Seletor[0], ~Seletor[1], Seletor[2], ~Seletor[3], ~Seletor[4]);  // AND_Gate
  or or_1 (or_1_out, and_2_out, and_3_out);
  and and_2 (and_2_out, a, b, ~s);  // AND_Gate
  and and_3 (and_3_out, ~a, ~b, s);  // AND_Gate

  // Notes on the sheet:
  //   00100 - Soma de Naturais
  //   00101 - Soma de Inteiros
endmodule

module Somador (
  input  Vem1,
  input  a,
  input  b,
  output S,
  output Vai1
);

  wire and_1_out, and_2_out, and_3_out, xor_1_out;

  and and_1 (and_1_out, b, a);
  and and_2 (and_2_out, b, Vem1);
  or or_1 (Vai1, and_1_out, and_2_out, and_3_out);
  and and_3 (and_3_out, a, Vem1);
  xor xor_1 (xor_1_out, a, b);
  xor xor_2 (S, Vem1, xor_1_out);
endmodule

module Subtrator (
  input  Vem1,
  input  a,
  input  b,
  output S,
  output Vai1
);

  wire and_1_out, and_2_out, and_3_out, xor_1_out;

  and and_1 (and_1_out, b, ~a);  // AND_Gate
  and and_2 (and_2_out, b, Vem1);
  or or_1 (Vai1, and_1_out, and_2_out, and_3_out);
  and and_3 (and_3_out, ~a, Vem1);  // AND_Gate
  xor xor_1 (xor_1_out, a, b);
  xor xor_2 (S, Vem1, xor_1_out);
endmodule
